# Fritzing sketch Sensor_Node_Schematic (saved by Fritzing 1.0.8)
# 18650 Li-ion Battery: CC-BY Dr Kristofer Chan, King's College London/Remote-research.org
breadboards: 1

parts:
  M2 = TP4056 Module [part_number=HW-107]
  A2 = GY-SHT30 Breakout
  BAT1 = 18650 Li-ion Battery [package=battery-18650]
  R2 = Resistor [tolerance=±5% power=0.25W resistance=1M package=THT]
  R1 = Resistor [tolerance=±5% power=0.25W resistance=1M package=THT]
  A1 = Esp32-c3 super mini
  C1 = Ceramic Capacitor [capacitance=100nF voltage=35V package="100 mil [THT, multilayer]"]

nets:
  N1: M2.OUT-#1, A2.Pin_2, R1.Pin_1, A1.Pin_15, C1.0
  N2: M2.BAT-, BAT1.-
  N3: M2.BAT+, BAT1.+
  N4: M2.OUT-#4, R2.Pin_0, A1.Pin_16
  N5: A2.Pin_1, A1.Pin_14
  N6: A2.Pin_3, A1.Pin_13
  N7: A2.Pin_4, A1.Pin_12
  N8: R2.Pin_1, R1.Pin_0, A1.Pin_9, C1.1

custom parts:
  TP4056 Module: TP4056 Lithium Battery Charge Management Module Links: TP4056 website
  18650 Li-ion Battery: 18650 li-ion Battery Standard 18650 battery with interactive connectors Creative Common Attribution 4.0 International (CC-BY 4.0) license. Any use of this part requires attribution of Dr Kristofer Chan, Department of Geography, King's College London. Contact kristofer.chan [at] kcl.ac.uk OR kris [at] remote-research.org for further information.
  Esp32-c3 super mini: ESP32-C3 Development Board ESP32 SuperMini Development Board ESP32 Development Board WiFi Bluetooth.
